// Logisim project control-logic.circ as structural Verilog: 1 circuit, main circuit control_logic
module control_logic (
  input  [31:0] inst,
  input  BrEq,
  input  BrLt,
  output PCSel,
  output RegWEn,
  output [2:0] ImmSel,
  output BrUn,
  output ASel,
  output BSel,
  output [3:0] ALUSel,
  output MemRW,
  output [1:0] WBSel,
  output CSRSel,
  output CSRWen,
  output [5:0] out_15
);

  wire and_1_out, and_2_out, and_3_out, and_4_out, and_5_out, and_6_out, and_7_out, and_8_out, and_9_out,
       and_10_out, func3_000, func3_001, func3_010, func3_011, func3_100, func3_101, func3_110, func3_111,
       func7_0b0000000, func7_0b0100000, opcode_0b0010011;
  wire [3:0] priority_encoder_1_out;
  wire [5:0] bit_extender_1_out;

  Comparator #(.mode("unsigned"), .width(7)) comparator_1 (
    .a(inst[6:0]), .b(7'b0010011), .eq(opcode_0b0010011));  // open: gt, lt
  ROM #(.addrWidth(6), .dataWidth(16)) rom_1 (
    .addr(out_15), .data({RegWEn, ImmSel, BrUn, ASel, BSel, ALUSel, MemRW, WBSel, CSRSel, CSRWen}));
  Comparator #(.mode("unsigned"), .width(3)) comparator_2 (
    .a(inst[14:12]), .b(3'b000), .eq(func3_000));  // open: gt, lt
  Comparator #(.mode("unsigned"), .width(3)) comparator_3 (
    .a(inst[14:12]), .b(3'b001), .eq(func3_001));  // open: gt, lt
  Comparator #(.mode("unsigned"), .width(3)) comparator_4 (
    .a(inst[14:12]), .b(3'b010), .eq(func3_010));  // open: gt, lt
  Comparator #(.mode("unsigned"), .width(3)) comparator_5 (
    .a(inst[14:12]), .b(3'b011), .eq(func3_011));  // open: gt, lt
  Comparator #(.mode("unsigned"), .width(3)) comparator_6 (
    .a(inst[14:12]), .b(3'b100), .eq(func3_100));  // open: gt, lt
  Comparator #(.mode("unsigned"), .width(3)) comparator_7 (
    .a(inst[14:12]), .b(3'b101), .eq(func3_101));  // open: gt, lt
  Comparator #(.mode("unsigned"), .width(3)) comparator_8 (
    .a(inst[14:12]), .b(3'b110), .eq(func3_110));  // open: gt, lt
  Comparator #(.mode("unsigned"), .width(3)) comparator_9 (
    .a(inst[14:12]), .b(3'b111), .eq(func3_111));  // open: gt, lt
  Comparator #(.mode("unsigned"), .width(7)) comparator_10 (
    .a(inst[31:25]), .b({7{1'b0}}), .eq(func7_0b0000000));  // open: gt, lt
  Comparator #(.mode("unsigned"), .width(7)) comparator_11 (
    .a(inst[31:25]), .b(7'b0100000), .eq(func7_0b0100000));  // open: gt, lt
  and and_1 (and_1_out, opcode_0b0010011, func3_000);
  and and_2 (and_2_out, opcode_0b0010011, func3_001);
  and and_3 (and_3_out, opcode_0b0010011, func3_010);
  and and_4 (and_4_out, opcode_0b0010011, func3_100);
  and and_5 (and_5_out, opcode_0b0010011, func3_101);
  and and_6 (and_6_out, opcode_0b0010011, func3_110);
  and and_7 (and_7_out, opcode_0b0010011, func3_111);
  and and_8 (and_8_out, and_2_out, func7_0b0000000);
  and and_9 (and_9_out, func7_0b0000000, and_5_out);
  and and_10 (and_10_out, and_5_out, func7_0b0100000);
  Priority_Encoder #(.select(4)) priority_encoder_1 (
    .in0(and_1_out), .in1(and_8_out), .in2(and_3_out), .in3(and_4_out), .in4(and_9_out), .in5(and_10_out),
    .in6(and_6_out), .in7(and_7_out), .out(priority_encoder_1_out));  // open: in8, in9, in10, in11, in12, in13, in14, in15, gs, en_out, en_in
  assign bit_extender_1_out = {{2{1'b0}}, priority_encoder_1_out};  // Bit_Extender bit_extender_1
  Adder #(.width(6)) adder_1 (.a(bit_extender_1_out), .b(6'b001111), .out(out_15));  // open: cin, cout

  assign PCSel = 1'b1;

  // Other names for the same wires on the sheet: opcode[6:0] = inst[6:0]; func3[2:0] = inst[14:12];
  //   func7[6:0] = inst[31:25]; ROM_INPUT[5:0] = out_15

  // Notes on the sheet:
  //   I type, opcode = 0b0010011
  //   INPUTS to your circuit
  //   Connect ROM Input here ->
  //   contents of rom_1 (hex, n*v repeats v):
  //   15*0 9204 9224 9244 9284 92a4 93a4 92c4 92e4
  //   ROM FOR CONTROL LOGIC
  //   func3 = 0
  //   func7 = 0
  //   DON'T CHANGE THE LOCATIONS OF THE INPUTS AND OUTPUTS!
  //   OUTPUT from your circuit
  //   CLOSE
  //   WIRE
  //   TO
  //   USE
  //   ROM
  //   Reminder: Use combinational logic for PCSel
  //   I type
endmodule
